// Logisim project project.circ as structural Verilog: 11 circuits, main circuit main
module main (
  input  Clear,
  input  in_2
);

  wire ALU_Signal, CF, Clock, CMP_Signal, JMP_Signal, LD_Signal, not_1_out, RegisterWriteSignal, ST_Signal,
       ZF;
  wire [2:0] DR, multiplexer_3_out, SR1, SR2;
  wire [3:0] OpCode;
  wire [9:0] LD_ST_ADDRESS;
  wire [15:0] adder_1_sum, ALU_Result, DataLoaded, IMM, JMPAddr, multiplexer_1_out, multiplexer_2_out,
       Output1, Output2, PC_q, rom_1_data;

  Clock clock_1 (.out(Clock));
  Multiplexer #(.width(16), .enable("false")) multiplexer_1 (
    .in0(16'h1), .in1(JMPAddr), .out(multiplexer_1_out), .sel(JMP_Signal));
  Adder adder_1 (.B(multiplexer_1_out), .A(PC_q), .Sum(adder_1_sum));  // open: Carry_out
  CMP cmp_1 (.A(Output1), .B(Output2), .CF(CF), .ZF(ZF), .CMP_Signal(CMP_Signal), .Clock(Clock));
  Register #(.width(16)) PC (.D(adder_1_sum), .en(1'b1), .Q(PC_q), .clk(Clock), .clr(Clear));
  ALU alu_1 (
    .SR1(Output1), .SR2(Output2), .IMM(IMM), .ALU_Result(ALU_Result), .OpCode(OpCode), .ALU_Signal(ALU_Signal));
  ROM #(.addrWidth(16), .dataWidth(16)) rom_1 (.addr(PC_q), .data(rom_1_data), .sel(1'b1));
  Control_Unit control_unit_1 (
    .SR1(SR1), .SR2(SR2), .DR(DR), .OpCodeOut(OpCode), .LD_ST_ADDRESS(LD_ST_ADDRESS),
    .RegisterWrite(RegisterWriteSignal), .ALU_Signal(ALU_Signal), .LD_Signal(LD_Signal),
    .ST_Signal(ST_Signal), .CMP_SIGNAL(CMP_Signal), .Instruction(rom_1_data), .IMM(IMM), .ZF(ZF), .CF(CF),
    .JMP_Signal(JMP_Signal), .JumpAddress(JMPAddr));
  Multiplexer #(.width(16), .enable("false")) multiplexer_2 (
    .in0(DataLoaded), .in1(ALU_Result), .out(multiplexer_2_out), .sel(not_1_out));
  not not_1 (not_1_out, LD_Signal);
  Multiplexer #(.width(3), .enable("false")) multiplexer_3 (
    .in0(SR1), .in1(DR), .out(multiplexer_3_out), .sel(ST_Signal));
  RAM #(.addrWidth(10), .dataWidth(16), .bus("separate")) ram_1 (
    .addr(LD_ST_ADDRESS), .din(Output1), .data(DataLoaded), .str(ST_Signal), .sel(1'b1), .clk(Clock),
    .ld(LD_Signal), .clr(in_2));
  RegisterFile registerfile_1 (
    .rd1(multiplexer_3_out), .rd2(SR2), .input_data(multiplexer_2_out), .Write(DR), .Clock(Clock),
    .output_data_2(Output2), .output_data_1(Output1), .WE(RegisterWriteSignal));

  // Notes on the sheet:
  //   Instruction Memory
  //   contents of rom_1 (hex, n*v repeats v):
  //   4602 4802 2c42 34fb ac4 5c04 6023 8ffe
  //   Data Memory
endmodule

module Adder (
  input  [15:0] B,
  input  [15:0] A,
  output Carry_out,
  output [15:0] Sum
);

  wire fulladder_2_carry_out, fulladder_3_carry_out, fulladder_4_carry_out, fulladder_5_carry_out,
       fulladder_6_carry_out, fulladder_7_carry_out, fulladder_8_carry_out, fulladder_9_carry_out,
       fulladder_10_carry_out, fulladder_11_carry_out, fulladder_12_carry_out, fulladder_13_carry_out,
       fulladder_14_carry_out, fulladder_15_carry_out, fulladder_16_carry_out;

  FullAdder fulladder_1 (.A(A[15]), .B(B[15]), .Carry_in(fulladder_2_carry_out), .Sum(Sum[15]), .Carry_out(Carry_out));
  FullAdder fulladder_2 (
    .A(A[14]), .B(B[14]), .Carry_in(fulladder_3_carry_out), .Sum(Sum[14]), .Carry_out(fulladder_2_carry_out));
  FullAdder fulladder_3 (
    .A(A[13]), .B(B[13]), .Carry_in(fulladder_4_carry_out), .Sum(Sum[13]), .Carry_out(fulladder_3_carry_out));
  FullAdder fulladder_4 (
    .A(A[12]), .B(B[12]), .Carry_in(fulladder_5_carry_out), .Sum(Sum[12]), .Carry_out(fulladder_4_carry_out));
  FullAdder fulladder_5 (
    .A(A[11]), .B(B[11]), .Carry_in(fulladder_6_carry_out), .Sum(Sum[11]), .Carry_out(fulladder_5_carry_out));
  FullAdder fulladder_6 (
    .A(A[10]), .B(B[10]), .Carry_in(fulladder_7_carry_out), .Sum(Sum[10]), .Carry_out(fulladder_6_carry_out));
  FullAdder fulladder_7 (
    .A(A[9]), .B(B[9]), .Carry_in(fulladder_8_carry_out), .Sum(Sum[9]), .Carry_out(fulladder_7_carry_out));
  FullAdder fulladder_8 (
    .A(A[8]), .B(B[8]), .Carry_in(fulladder_9_carry_out), .Sum(Sum[8]), .Carry_out(fulladder_8_carry_out));
  FullAdder fulladder_9 (
    .A(A[7]), .B(B[7]), .Carry_in(fulladder_10_carry_out), .Sum(Sum[7]), .Carry_out(fulladder_9_carry_out));
  FullAdder fulladder_10 (
    .A(A[6]), .B(B[6]), .Carry_in(fulladder_11_carry_out), .Sum(Sum[6]), .Carry_out(fulladder_10_carry_out));
  FullAdder fulladder_11 (
    .A(A[5]), .B(B[5]), .Carry_in(fulladder_12_carry_out), .Sum(Sum[5]), .Carry_out(fulladder_11_carry_out));
  FullAdder fulladder_12 (
    .A(A[4]), .B(B[4]), .Carry_in(fulladder_13_carry_out), .Sum(Sum[4]), .Carry_out(fulladder_12_carry_out));
  FullAdder fulladder_13 (
    .A(A[3]), .B(B[3]), .Carry_in(fulladder_14_carry_out), .Sum(Sum[3]), .Carry_out(fulladder_13_carry_out));
  FullAdder fulladder_14 (
    .A(A[2]), .B(B[2]), .Carry_in(fulladder_15_carry_out), .Sum(Sum[2]), .Carry_out(fulladder_14_carry_out));
  FullAdder fulladder_15 (
    .A(A[1]), .B(B[1]), .Carry_in(fulladder_16_carry_out), .Sum(Sum[1]), .Carry_out(fulladder_15_carry_out));
  FullAdder fulladder_16 (.A(A[0]), .B(B[0]), .Carry_in(1'b0), .Sum(Sum[0]), .Carry_out(fulladder_16_carry_out));
endmodule

module FullAdder (
  input  A,
  input  B,
  input  Carry_in,
  output Sum,
  output Carry_out
);

  wire and_1_out, and_2_out, xor_1_out;

  xor xor_1 (xor_1_out, A, B);
  and and_1 (and_1_out, Carry_in, xor_1_out);
  and and_2 (and_2_out, A, B);
  xor xor_2 (Sum, xor_1_out, Carry_in);
  or or_1 (Carry_out, and_1_out, and_2_out);
endmodule

module PC (
  input  [15:0] JMPAddr,
  input  JMP_Signal,
  input  [15:0] PCAddr,
  input  Clear,
  input  Clock
);

  wire [15:0] adder_1_sum, multiplexer_1_out;

  Multiplexer #(.width(16), .enable("false")) multiplexer_1 (
    .in0(16'h1), .in1(JMPAddr), .out(multiplexer_1_out), .sel(JMP_Signal));
  Adder adder_1 (.B(multiplexer_1_out), .A(PCAddr), .Sum(adder_1_sum));  // open: Carry_out
  Register #(.width(16)) PC (.D(adder_1_sum), .en(1'b1), .Q(PCAddr), .clk(Clock), .clr(Clear));
endmodule

// H.C
module half_comparator (
  input  A,
  input  B,
  output gt,
  output lt,
  output eq
);

  wire not_1_out, not_2_out;

  not not_1 (not_1_out, B);
  not not_2 (not_2_out, A);
  and and_1 (gt, A, not_1_out);
  and and_2 (lt, not_2_out, B);
  xnor xnor_1 (eq, A, B);
endmodule

// F.C
module full_comparator (
  input  A,
  input  B,
  input  gt_in,
  input  lt_in,
  input  eq_in,
  output gt_out,
  output lt_out,
  output eq_out
);

  wire and_1_out, and_2_out, not_1_out, not_2_out, xnor_1_out;

  not not_1 (not_1_out, A);
  not not_2 (not_2_out, B);
  and and_1 (and_1_out, A, not_2_out, eq_in);
  and and_2 (and_2_out, not_1_out, B, eq_in);
  xnor xnor_1 (xnor_1_out, A, B);
  or or_1 (gt_out, and_1_out, gt_in);
  or or_2 (lt_out, and_2_out, lt_in);
  and and_3 (eq_out, eq_in, xnor_1_out);
endmodule

module _16bit_comparator (
  input  [15:0] op1,
  input  [15:0] op2,
  output gt,
  output lt,
  output eq
);

  wire full_comparator_1_eq_out, full_comparator_1_gt_out, full_comparator_1_lt_out,
       full_comparator_2_eq_out, full_comparator_2_gt_out, full_comparator_2_lt_out,
       full_comparator_3_eq_out, full_comparator_3_gt_out, full_comparator_3_lt_out,
       full_comparator_4_eq_out, full_comparator_4_gt_out, full_comparator_4_lt_out,
       full_comparator_5_eq_out, full_comparator_5_gt_out, full_comparator_5_lt_out,
       full_comparator_6_eq_out, full_comparator_6_gt_out, full_comparator_6_lt_out,
       full_comparator_7_eq_out, full_comparator_7_gt_out, full_comparator_7_lt_out,
       full_comparator_8_eq_out, full_comparator_8_gt_out, full_comparator_8_lt_out,
       full_comparator_9_eq_out, full_comparator_9_gt_out, full_comparator_9_lt_out,
       full_comparator_10_eq_out, full_comparator_10_gt_out, full_comparator_10_lt_out,
       full_comparator_11_eq_out, full_comparator_11_gt_out, full_comparator_11_lt_out,
       full_comparator_12_eq_out, full_comparator_12_gt_out, full_comparator_12_lt_out,
       full_comparator_13_eq_out, full_comparator_13_gt_out, full_comparator_13_lt_out,
       full_comparator_14_eq_out, full_comparator_14_gt_out, full_comparator_14_lt_out, half_comparator_1_eq,
       half_comparator_1_gt, half_comparator_1_lt;

  half_comparator half_comparator_1 (
    .A(op1[15]), .B(op2[15]), .gt(half_comparator_1_gt), .lt(half_comparator_1_lt), .eq(half_comparator_1_eq));
  full_comparator full_comparator_1 (
    .A(op1[14]), .B(op2[14]), .gt_in(half_comparator_1_gt), .lt_in(half_comparator_1_lt),
    .eq_in(half_comparator_1_eq), .gt_out(full_comparator_1_gt_out), .lt_out(full_comparator_1_lt_out),
    .eq_out(full_comparator_1_eq_out));
  full_comparator full_comparator_2 (
    .A(op1[13]), .B(op2[13]), .gt_in(full_comparator_1_gt_out), .lt_in(full_comparator_1_lt_out),
    .eq_in(full_comparator_1_eq_out), .gt_out(full_comparator_2_gt_out), .lt_out(full_comparator_2_lt_out),
    .eq_out(full_comparator_2_eq_out));
  full_comparator full_comparator_3 (
    .A(op1[11]), .B(op2[11]), .gt_in(full_comparator_4_gt_out), .lt_in(full_comparator_4_lt_out),
    .eq_in(full_comparator_4_eq_out), .gt_out(full_comparator_3_gt_out), .lt_out(full_comparator_3_lt_out),
    .eq_out(full_comparator_3_eq_out));
  full_comparator full_comparator_4 (
    .A(op1[12]), .B(op2[12]), .gt_in(full_comparator_2_gt_out), .lt_in(full_comparator_2_lt_out),
    .eq_in(full_comparator_2_eq_out), .gt_out(full_comparator_4_gt_out), .lt_out(full_comparator_4_lt_out),
    .eq_out(full_comparator_4_eq_out));
  full_comparator full_comparator_5 (
    .A(op1[10]), .B(op2[10]), .gt_in(full_comparator_3_gt_out), .lt_in(full_comparator_3_lt_out),
    .eq_in(full_comparator_3_eq_out), .gt_out(full_comparator_5_gt_out), .lt_out(full_comparator_5_lt_out),
    .eq_out(full_comparator_5_eq_out));
  full_comparator full_comparator_6 (
    .A(op1[9]), .B(op2[9]), .gt_in(full_comparator_5_gt_out), .lt_in(full_comparator_5_lt_out),
    .eq_in(full_comparator_5_eq_out), .gt_out(full_comparator_6_gt_out), .lt_out(full_comparator_6_lt_out),
    .eq_out(full_comparator_6_eq_out));
  full_comparator full_comparator_7 (
    .A(op1[8]), .B(op2[8]), .gt_in(full_comparator_6_gt_out), .lt_in(full_comparator_6_lt_out),
    .eq_in(full_comparator_6_eq_out), .gt_out(full_comparator_7_gt_out), .lt_out(full_comparator_7_lt_out),
    .eq_out(full_comparator_7_eq_out));
  full_comparator full_comparator_8 (
    .A(op1[6]), .B(op2[6]), .gt_in(full_comparator_9_gt_out), .lt_in(full_comparator_9_lt_out),
    .eq_in(full_comparator_9_eq_out), .gt_out(full_comparator_8_gt_out), .lt_out(full_comparator_8_lt_out),
    .eq_out(full_comparator_8_eq_out));
  full_comparator full_comparator_9 (
    .A(op1[7]), .B(op2[7]), .gt_in(full_comparator_7_gt_out), .lt_in(full_comparator_7_lt_out),
    .eq_in(full_comparator_7_eq_out), .gt_out(full_comparator_9_gt_out), .lt_out(full_comparator_9_lt_out),
    .eq_out(full_comparator_9_eq_out));
  full_comparator full_comparator_10 (
    .A(op1[5]), .B(op2[5]), .gt_in(full_comparator_8_gt_out), .lt_in(full_comparator_8_lt_out),
    .eq_in(full_comparator_8_eq_out), .gt_out(full_comparator_10_gt_out), .lt_out(full_comparator_10_lt_out),
    .eq_out(full_comparator_10_eq_out));
  full_comparator full_comparator_11 (
    .A(op1[4]), .B(op2[4]), .gt_in(full_comparator_10_gt_out), .lt_in(full_comparator_10_lt_out),
    .eq_in(full_comparator_10_eq_out), .gt_out(full_comparator_11_gt_out),
    .lt_out(full_comparator_11_lt_out), .eq_out(full_comparator_11_eq_out));
  full_comparator full_comparator_12 (
    .A(op1[2]), .B(op2[2]), .gt_in(full_comparator_13_gt_out), .lt_in(full_comparator_13_lt_out),
    .eq_in(full_comparator_13_eq_out), .gt_out(full_comparator_12_gt_out),
    .lt_out(full_comparator_12_lt_out), .eq_out(full_comparator_12_eq_out));
  full_comparator full_comparator_13 (
    .A(op1[3]), .B(op2[3]), .gt_in(full_comparator_11_gt_out), .lt_in(full_comparator_11_lt_out),
    .eq_in(full_comparator_11_eq_out), .gt_out(full_comparator_13_gt_out),
    .lt_out(full_comparator_13_lt_out), .eq_out(full_comparator_13_eq_out));
  full_comparator full_comparator_14 (
    .A(op1[1]), .B(op2[1]), .gt_in(full_comparator_12_gt_out), .lt_in(full_comparator_12_lt_out),
    .eq_in(full_comparator_12_eq_out), .gt_out(full_comparator_14_gt_out),
    .lt_out(full_comparator_14_lt_out), .eq_out(full_comparator_14_eq_out));
  full_comparator full_comparator_15 (
    .A(op1[0]), .B(op2[0]), .gt_in(full_comparator_14_gt_out), .lt_in(full_comparator_14_lt_out),
    .eq_in(full_comparator_14_eq_out), .gt_out(gt), .lt_out(lt), .eq_out(eq));
endmodule

module CMP (
  input  [15:0] A,
  input  [15:0] B,
  input  CMP_Signal,
  input  Clock,
  output CF,
  output ZF
);

  wire and_1_out, and_2_out, n16bit_comparator_1_eq, n16bit_comparator_1_gt, n16bit_comparator_1_lt,
       not_1_out, not_2_out, not_3_out;

  not not_1 (not_1_out, n16bit_comparator_1_gt);
  _16bit_comparator u_16bit_comparator_1 (
    .op1(A), .op2(B), .gt(n16bit_comparator_1_gt), .lt(n16bit_comparator_1_lt), .eq(n16bit_comparator_1_eq));
  not not_2 (not_2_out, n16bit_comparator_1_eq);
  not not_3 (not_3_out, n16bit_comparator_1_lt);
  and and_1 (and_1_out, not_1_out, n16bit_comparator_1_lt, not_2_out);
  and and_2 (and_2_out, not_1_out, not_3_out, n16bit_comparator_1_eq);
  Register #(.width(1)) Reg_CF (.D(and_1_out), .en(CMP_Signal), .Q(CF), .clk(Clock));  // open: clr
  Register #(.width(1)) Reg_ZF (.D(and_2_out), .en(CMP_Signal), .Q(ZF), .clk(Clock));  // open: clr
endmodule

// Register File
module RegisterFile (
  input  [2:0] rd1,
  input  [2:0] rd2,
  input  [15:0] input_data,
  input  [2:0] Write,
  input  Clock,
  input  WE,
  output [15:0] output_data_2,
  output [15:0] output_data_1
);

  wire and_1_out, and_2_out, and_3_out, and_4_out, and_5_out, and_6_out, and_7_out, and_8_out,
       decoder_1_out0, decoder_1_out1, decoder_1_out2, decoder_1_out3, decoder_1_out4, decoder_1_out5,
       decoder_1_out6, decoder_1_out7, decoder_2_out0, decoder_2_out1, decoder_2_out2, decoder_2_out3,
       decoder_2_out4, decoder_2_out5, decoder_2_out6, decoder_2_out7, decoder_3_out0, decoder_3_out1,
       decoder_3_out2, decoder_3_out3, decoder_3_out4, decoder_3_out5, decoder_3_out6, decoder_3_out7;
  wire [15:0] register_1_q, register_2_q, register_3_q, register_4_q, register_5_q, register_6_q,
       register_7_q, register_8_q;

  Decoder #(.select(3), .enable("false")) decoder_1 (
    .out0(decoder_1_out0), .out1(decoder_1_out1), .out2(decoder_1_out2), .out3(decoder_1_out3),
    .out4(decoder_1_out4), .out5(decoder_1_out5), .out6(decoder_1_out6), .out7(decoder_1_out7), .sel(rd1));
  Decoder #(.select(3), .enable("false")) decoder_2 (
    .out0(decoder_2_out0), .out1(decoder_2_out1), .out2(decoder_2_out2), .out3(decoder_2_out3),
    .out4(decoder_2_out4), .out5(decoder_2_out5), .out6(decoder_2_out6), .out7(decoder_2_out7), .sel(rd2));
  Decoder #(.select(3), .enable("false")) decoder_3 (
    .out0(decoder_3_out0), .out1(decoder_3_out1), .out2(decoder_3_out2), .out3(decoder_3_out3),
    .out4(decoder_3_out4), .out5(decoder_3_out5), .out6(decoder_3_out6), .out7(decoder_3_out7), .sel(Write));
  and and_1 (and_1_out, decoder_3_out0, WE);
  and and_2 (and_2_out, decoder_3_out1, decoder_3_out1, WE);
  and and_3 (and_3_out, decoder_3_out2, WE);
  and and_4 (and_4_out, decoder_3_out3, WE);
  and and_5 (and_5_out, decoder_3_out4, WE);
  and and_6 (and_6_out, decoder_3_out5, WE);
  and and_7 (and_7_out, decoder_3_out6, WE);
  and and_8 (and_8_out, decoder_3_out7, WE);
  Register #(.width(16)) register_1 (.D(input_data), .en(and_1_out), .Q(register_1_q), .clk(Clock), .clr(1'b0));
  Register #(.width(16)) register_2 (.D(input_data), .en(and_2_out), .Q(register_2_q), .clk(Clock), .clr(1'b0));
  Register #(.width(16)) register_3 (.D(input_data), .en(and_3_out), .Q(register_3_q), .clk(Clock), .clr(1'b0));
  Register #(.width(16)) register_4 (.D(input_data), .en(and_4_out), .Q(register_4_q), .clk(Clock), .clr(1'b0));
  Register #(.width(16)) register_5 (.D(input_data), .en(and_5_out), .Q(register_5_q), .clk(Clock), .clr(1'b0));
  Register #(.width(16)) register_6 (.D(input_data), .en(and_6_out), .Q(register_6_q), .clk(Clock), .clr(1'b0));
  Register #(.width(16)) register_7 (.D(input_data), .en(and_7_out), .Q(register_7_q), .clk(Clock), .clr(1'b0));
  Register #(.width(16)) register_8 (.D(input_data), .en(and_8_out), .Q(register_8_q), .clk(Clock), .clr(1'b0));
  assign output_data_2 = decoder_2_out0 ? register_1_q : 16'bz;  // Controlled_Buffer controlled_buffer_1
  assign output_data_1 = decoder_1_out0 ? register_1_q : 16'bz;  // Controlled_Buffer controlled_buffer_2
  assign output_data_2 = decoder_2_out1 ? register_2_q : 16'bz;  // Controlled_Buffer controlled_buffer_3
  assign output_data_1 = decoder_1_out1 ? register_2_q : 16'bz;  // Controlled_Buffer controlled_buffer_4
  assign output_data_2 = decoder_2_out2 ? register_3_q : 16'bz;  // Controlled_Buffer controlled_buffer_5
  assign output_data_1 = decoder_1_out2 ? register_3_q : 16'bz;  // Controlled_Buffer controlled_buffer_6
  assign output_data_2 = decoder_2_out3 ? register_4_q : 16'bz;  // Controlled_Buffer controlled_buffer_7
  assign output_data_1 = decoder_1_out3 ? register_4_q : 16'bz;  // Controlled_Buffer controlled_buffer_8
  assign output_data_2 = decoder_2_out4 ? register_5_q : 16'bz;  // Controlled_Buffer controlled_buffer_9
  assign output_data_1 = decoder_1_out4 ? register_5_q : 16'bz;  // Controlled_Buffer controlled_buffer_10
  assign output_data_2 = decoder_2_out5 ? register_6_q : 16'bz;  // Controlled_Buffer controlled_buffer_11
  assign output_data_1 = decoder_1_out5 ? register_6_q : 16'bz;  // Controlled_Buffer controlled_buffer_12
  assign output_data_2 = decoder_2_out6 ? register_7_q : 16'bz;  // Controlled_Buffer controlled_buffer_13
  assign output_data_1 = decoder_1_out6 ? register_7_q : 16'bz;  // Controlled_Buffer controlled_buffer_14
  assign output_data_2 = decoder_2_out7 ? register_8_q : 16'bz;  // Controlled_Buffer controlled_buffer_15
  assign output_data_1 = decoder_1_out7 ? register_8_q : 16'bz;  // Controlled_Buffer controlled_buffer_16
endmodule

module ALU (
  input  [15:0] SR1,
  input  [15:0] SR2,
  input  [15:0] IMM,
  input  ALU_Signal,
  input  [3:0] OpCode,
  output [15:0] ALU_Result
);

  wire and_1_out, and_3_out;
  wire [15:0] adder_1_sum, and_2_out, multiplexer_1_out;

  Multiplexer #(.width(16), .enable("false")) multiplexer_1 (
    .in0(SR2), .in1(IMM), .out(multiplexer_1_out), .sel(and_1_out));
  and and_1 (and_1_out, ALU_Signal, OpCode[0]);
  assign and_2_out = SR1 & multiplexer_1_out;  // AND_Gate and_2, 16 bits wide
  Adder adder_1 (.B(multiplexer_1_out), .A(SR1), .Sum(adder_1_sum));  // open: Carry_out
  and and_3 (and_3_out, ALU_Signal, OpCode[1]);
  Multiplexer #(.width(16), .enable("false")) multiplexer_2 (
    .in0(and_2_out), .in1(adder_1_sum), .out(ALU_Result), .sel(and_3_out));
endmodule

module Control_Unit (
  input  [15:0] Instruction,
  input  ZF,
  input  CF,
  output [15:0] JumpAddress,
  output [15:0] IMM,
  output [2:0] SR1,
  output [2:0] SR2,
  output [2:0] DR,
  output [3:0] OpCodeOut,
  output [9:0] LD_ST_ADDRESS,
  output RegisterWrite,
  output JMP_Signal,
  output ALU_Signal,
  output LD_Signal,
  output ST_Signal,
  output CMP_SIGNAL
);

  wire ADD, ADDI, AND, and_1_out, and_2_out, and_3_out, and_4_out, and_5_out, and_6_out, and_7_out,
       and_8_out, and_9_out, and_10_out, ANDI, JA, JAE, JB, JBE, JE, JUMP, not_1_out, not_2_out, or_3_out,
       or_4_out;

  Decoder #(.select(4)) decoder_1 (
    .out0(AND), .out1(ANDI), .out2(ADD), .out3(ADDI), .out4(LD_Signal), .out5(ST_Signal), .out6(CMP_SIGNAL),
    .out7(JUMP), .out8(JE), .out9(JA), .out10(JB), .out11(JBE), .out12(JAE), .sel(Instruction[15:12]));  // open: out13, out14, out15, en
  assign JumpAddress = {{4{Instruction[11]}}, Instruction[11:0]};  // Bit_Extender bit_extender_1
  or or_1 (RegisterWrite, ANDI, ADDI, AND, ADD, LD_Signal);
  or or_2 (ALU_Signal, ANDI, ADDI, AND, ADD);
  assign LD_ST_ADDRESS = {{1{1'b0}}, Instruction[8:0]};  // Bit_Extender bit_extender_2
  assign IMM = {{10{Instruction[5]}}, Instruction[5:0]};  // Bit_Extender bit_extender_3
  not not_1 (not_1_out, ZF);
  not not_2 (not_2_out, CF);
  and and_1 (and_1_out, not_1_out, not_2_out);
  and and_2 (and_2_out, not_2_out, ZF);
  and and_3 (and_3_out, ZF, not_2_out);
  and and_4 (and_4_out, not_1_out, not_2_out);
  and and_5 (and_5_out, not_1_out, CF);
  or or_3 (or_3_out, and_1_out, and_2_out);
  or or_4 (or_4_out, ZF, CF);
  and and_6 (and_6_out, and_3_out, JE);
  and and_7 (and_7_out, and_4_out, JA);
  and and_8 (and_8_out, and_5_out, JB);
  and and_9 (and_9_out, or_3_out, JAE);
  and and_10 (and_10_out, or_4_out, JBE);
  or or_5 (JMP_Signal, JUMP, and_6_out, and_7_out, and_8_out, and_9_out, and_10_out);

  assign DR = Instruction[11:9];
  assign OpCodeOut = Instruction[15:12];
  assign SR1 = Instruction[8:6];
  assign SR2 = Instruction[2:0];

  // Other names for the same wires on the sheet: CMP = CMP_SIGNAL; JumpAddress_t[11:0] = Instruction[11:0];
  //   IMM_t[5:0] = Instruction[5:0]; LD_ST_ADDRESS_t[8:0] = Instruction[8:0]; LD = LD_Signal;
  //   OpBit0 = Instruction[12]; OpCode[3:0] = Instruction[15:12]; OpBit1 = Instruction[13]; OpBit2 = Instruction[14];
  //   OpBit3 = Instruction[15]; ST = ST_Signal
endmodule
